// Logisim project 1_fns.circ as structural Verilog: 4 circuits, main circuit f1
module f1 (
  input  x1,
  input  x2,
  input  x3,
  output o1
);

  wire nand_1_out, nand_2_out, not_1_out, not_2_out, not_3_out;

  not not_1 (not_1_out, x2);
  not not_2 (not_2_out, x3);
  not not_3 (not_3_out, x1);
  nand nand_1 (nand_1_out, x1, not_1_out, not_2_out);
  nand nand_2 (nand_2_out, not_3_out, x2);
  nand nand_3 (o1, nand_1_out, nand_2_out);
endmodule

module f2 (
  input  in_1,
  input  in_2,
  output out_3
);

  wire and_1_out, and_2_out;

  and and_1 (and_1_out, ~in_1, ~in_2);  // AND_Gate
  and and_2 (and_2_out, in_1, in_2);
  or or_1 (out_3, and_1_out, and_2_out);
endmodule

module f4 (
  input  a,
  input  b,
  input  c,
  input  d,
  output x
);

  wire and_1_out, and_2_out, and_3_out, and_4_out, not_1_out, not_2_out, not_3_out, not_4_out;

  not not_1 (not_1_out, a);
  not not_2 (not_2_out, b);
  not not_3 (not_3_out, c);
  not not_4 (not_4_out, d);
  and and_1 (and_1_out, not_1_out, not_2_out, not_3_out);
  and and_2 (and_2_out, a, not_2_out, not_4_out);
  and and_3 (and_3_out, not_3_out, not_4_out);
  and and_4 (and_4_out, a, b, d);
  or or_1 (x, and_1_out, and_2_out, and_3_out, and_4_out);
endmodule

module f3 (
  input  in_1,
  input  x1,
  input  x2,
  input  x3,
  input  x4,
  output F
);

  wire nand_1_out, nand_2_out, nand_3_out, nand_4_out, nand_5_out, nand_6_out, nand_7_out, nand_8_out,
       nand_9_out;

  nand nand_1 (nand_1_out, in_1, x1);
  nand nand_2 (nand_2_out, in_1, x2);
  nand nand_3 (nand_3_out, in_1, x3);
  nand nand_4 (nand_4_out, in_1, x4);
  nand nand_5 (nand_5_out, nand_1_out, nand_4_out);
  nand nand_6 (nand_6_out, x1, nand_2_out, nand_3_out, x4);
  nand nand_7 (nand_7_out, nand_2_out, x3, nand_4_out);
  nand nand_8 (nand_8_out, x2, nand_3_out, nand_4_out);
  nand nand_9 (nand_9_out, x1, x2, x3, x4);
  nand nand_10 (F, nand_5_out, nand_6_out, nand_7_out, nand_8_out, nand_9_out);
endmodule
