// Logisim project 2_4bit_adder.circ as structural Verilog: 3 circuits, main circuit main
module main (
  input  C,
  input  [3:0] A,
  input  [3:0] B,
  output [3:0] out_4,
  output out_5
);

  wire full_adder_1_cout, full_adder_2_cout, full_adder_3_cout;

  full_adder full_adder_1 (.Cin(C), .A(A[0]), .B(B[0]), .Sum(out_4[0]), .Cout(full_adder_1_cout));
  full_adder full_adder_2 (.Cin(full_adder_1_cout), .A(A[1]), .B(B[1]), .Sum(out_4[1]), .Cout(full_adder_2_cout));
  full_adder full_adder_3 (.Cin(full_adder_2_cout), .A(A[2]), .B(B[2]), .Sum(out_4[2]), .Cout(full_adder_3_cout));
  full_adder full_adder_4 (.Cin(full_adder_3_cout), .A(A[3]), .B(B[3]), .Sum(out_4[3]), .Cout(out_5));
endmodule

module full_adder (
  input  Cin,
  input  A,
  input  B,
  output Sum,
  output Cout
);

  wire and_1_out, and_2_out, xor_1_out;

  xor xor_1 (xor_1_out, Cin, A);
  and and_1 (and_1_out, xor_1_out, A);
  and and_2 (and_2_out, Cin, A);
  xor xor_2 (Sum, xor_1_out, A);
  or or_1 (Cout, and_1_out, and_2_out);

  assign B = A;
endmodule

module half_adder (
  input  A,
  input  B,
  output S,
  output Cout
);

  xor xor_1 (S, A, B);
  and and_1 (Cout, A, B);
endmodule
