// Logisim project 4bit_16bit_adder.circ as structural Verilog: 6 circuits, main circuit main
module main (
  input  [3:0] FourBitA,
  input  [3:0] FourBitB,
  input  Cin,
  input  [15:0] HexA,
  input  [15:0] HexB,
  input  in_6,
  input  in_7,
  input  BitA,
  input  BitB,
  output [3:0] FourSum,
  output Cout1,
  output [15:0] HexSum,
  output Cout2,
  output out_14,
  output BitSum,
  output Cout3
);

  wire half_adder_1_cout;

  four_bit_half_adder four_bit_half_adder_1 (.FourBitA(FourBitA), .FourBitB(FourBitB), .Sum(FourSum), .Cout(Cout1));
  hex_full_adder hex_full_adder_1 (.Cin(Cin), .HexA(HexA), .HexB(HexB), .Sum(HexSum), .Cout(Cout2));
  half_adder half_adder_1 (.A(in_6), .B(in_7), .S(out_14), .Cout(half_adder_1_cout));
  full_adder full_adder_1 (.Cin(half_adder_1_cout), .A(BitA), .B(BitB), .Sum(BitSum), .Cout(Cout3));
endmodule

module full_adder (
  input  Cin,
  input  A,
  input  B,
  output Sum,
  output Cout
);

  wire and_1_out, and_2_out, xor_1_out;

  xor xor_1 (xor_1_out, Cin, A);
  xor xor_2 (Sum, xor_1_out, B);
  and and_1 (and_1_out, xor_1_out, B);
  or or_1 (Cout, and_1_out, and_2_out);
  and and_2 (and_2_out, Cin, A);
endmodule

module half_adder (
  input  A,
  input  B,
  output S,
  output Cout
);

  xor xor_1 (S, A, B);
  and and_1 (Cout, A, B);
endmodule

module four_bit_half_adder (
  input  [3:0] FourBitA,
  input  [3:0] FourBitB,
  output [3:0] Sum,
  output Cout
);

  wire full_adder_1_cout, full_adder_2_cout, half_adder_1_cout;

  half_adder half_adder_1 (.A(FourBitA[0]), .B(FourBitB[0]), .S(Sum[0]), .Cout(half_adder_1_cout));
  full_adder full_adder_1 (
    .Cin(half_adder_1_cout), .A(FourBitA[1]), .B(FourBitB[1]), .Sum(Sum[1]), .Cout(full_adder_1_cout));
  full_adder full_adder_2 (
    .Cin(full_adder_1_cout), .A(FourBitA[2]), .B(FourBitB[2]), .Sum(Sum[2]), .Cout(full_adder_2_cout));
  full_adder full_adder_3 (.Cin(full_adder_2_cout), .A(FourBitA[3]), .B(FourBitB[3]), .Sum(Sum[3]), .Cout(Cout));
endmodule

module hex_full_adder (
  input  Cin,
  input  [15:0] HexA,
  input  [15:0] HexB,
  output [15:0] Sum,
  output Cout
);

  wire four_bit_full_adder_1_cout, four_bit_full_adder_2_cout, four_bit_full_adder_3_cout;

  four_bit_full_adder four_bit_full_adder_1 (
    .Cin(Cin), .A(HexA[3:0]), .B(HexB[3:0]), .Sum(Sum[3:0]), .Cout(four_bit_full_adder_1_cout));
  four_bit_full_adder four_bit_full_adder_2 (
    .Cin(four_bit_full_adder_1_cout), .A(HexA[7:4]), .B(HexB[7:4]), .Sum(Sum[7:4]),
    .Cout(four_bit_full_adder_2_cout));
  four_bit_full_adder four_bit_full_adder_3 (
    .Cin(four_bit_full_adder_2_cout), .A(HexA[11:8]), .B(HexB[11:8]), .Sum(Sum[11:8]),
    .Cout(four_bit_full_adder_3_cout));
  four_bit_full_adder four_bit_full_adder_4 (
    .Cin(four_bit_full_adder_3_cout), .A(HexA[15:12]), .B(HexB[15:12]), .Sum(Sum[15:12]), .Cout(Cout));

  // Other names for the same wires on the sheet: A0[3:0] = HexA[3:0]; A1[3:0] = HexA[7:4]; A2[3:0] = HexA[11:8];
  //   A3[3:0] = HexA[15:12]; B0[3:0] = HexB[3:0]; B1[3:0] = HexB[7:4]; B2[3:0] = HexB[11:8]; B3[3:0] = HexB[15:12]
endmodule

module four_bit_full_adder (
  input  Cin,
  input  [3:0] A,
  input  [3:0] B,
  output [3:0] Sum,
  output Cout
);

  wire full_adder_1_cout, full_adder_2_cout, full_adder_3_cout;

  full_adder full_adder_1 (.Cin(Cin), .A(A[0]), .B(B[0]), .Sum(Sum[0]), .Cout(full_adder_1_cout));
  full_adder full_adder_2 (.Cin(full_adder_1_cout), .A(A[1]), .B(B[1]), .Sum(Sum[1]), .Cout(full_adder_2_cout));
  full_adder full_adder_3 (.Cin(full_adder_2_cout), .A(A[2]), .B(B[2]), .Sum(Sum[2]), .Cout(full_adder_3_cout));
  full_adder full_adder_4 (.Cin(full_adder_3_cout), .A(A[3]), .B(B[3]), .Sum(Sum[3]), .Cout(Cout));
endmodule
