// Logisim project 4-6.circ as structural Verilog: 2 circuits, main circuit D_Clock
module D_Clock (
  input  [3:0] in_1
);

  wire and_1_out, clock_1_out, d_ff_1_qn, d_ff_2_qn, d_ff_3_qn, d_ff_4_qn, Q0, Q1, Q2, Q3, xnor_1_out,
       xnor_2_out, xnor_3_out, xnor_4_out;

  D_Flip_Flop d_ff_1 (.D(d_ff_1_qn), .clk(clock_1_out), .Q(Q0), .Qn(d_ff_1_qn), .reset(and_1_out));  // open: preset
  Clock clock_1 (.out(clock_1_out));
  D_Flip_Flop d_ff_2 (.D(d_ff_2_qn), .clk(d_ff_1_qn), .Q(Q1), .Qn(d_ff_2_qn), .reset(and_1_out));  // open: preset
  xnor xnor_1 (xnor_1_out, Q0, in_1[0]);
  xnor xnor_2 (xnor_2_out, Q1, in_1[1]);
  xnor xnor_3 (xnor_3_out, Q2, in_1[2]);
  and and_1 (and_1_out, xnor_1_out, xnor_2_out, xnor_3_out, xnor_4_out);
  D_Flip_Flop d_ff_3 (.D(d_ff_3_qn), .clk(d_ff_2_qn), .Q(Q2), .Qn(d_ff_3_qn), .reset(and_1_out));  // open: preset
  xnor xnor_4 (xnor_4_out, Q3, in_1[3]);
  D_Flip_Flop d_ff_4 (.D(d_ff_4_qn), .clk(d_ff_3_qn), .Q(Q3), .Qn(d_ff_4_qn), .reset(and_1_out));  // open: preset
  Hex_Digit_Display hex_digit_display_1 (.value({Q3, Q2, Q1, Q0}));  // open: dp
endmodule

module T_three_clock (
  input  [3:0] in_1,
  input  in_2,
  input  [3:0] in_3,
  input  in_4,
  output [3:0] out_5,
  output [3:0] out_6,
  output [3:0] out_7
);

  wire and_1_out, clock_1_out, clock_2_out, Q0_qn, Q1_qn, Q2_qn, t_ff_1_qn, t_ff_2_qn, t_ff_3_qn;
  wire [3:0] Q0_q, t_ff_1_q;
  wire [7:4] main_1_out_3;

  T_Flip_Flop Q0 (.T(in_2), .clk(clock_1_out), .Q(Q0_q[0]), .Qn(Q0_qn), .reset(and_1_out));  // open: preset
  Clock clock_1 (.out(clock_1_out));
  T_Flip_Flop t_ff_1 (.T(in_4), .clk(clock_2_out), .Q(t_ff_1_q[0]), .Qn(t_ff_1_qn), .reset(out_7[1]));  // open: preset
  Clock clock_2 (.out(clock_2_out));
  T_Flip_Flop Q1 (.T(in_2), .clk(Q0_qn), .Q(Q0_q[1]), .Qn(Q1_qn), .reset(and_1_out));  // open: preset
  T_Flip_Flop t_ff_2 (.T(in_4), .clk(t_ff_1_qn), .Q(t_ff_1_q[1]), .Qn(t_ff_2_qn), .reset(out_7[1]));  // open: preset
  T_Flip_Flop Q2 (.T(in_2), .clk(Q1_qn), .Q(Q0_q[2]), .Qn(Q2_qn), .reset(and_1_out));  // open: preset
  T_Flip_Flop t_ff_3 (.T(in_4), .clk(t_ff_2_qn), .Q(t_ff_1_q[2]), .Qn(t_ff_3_qn), .reset(out_7[1]));  // open: preset
  T_Flip_Flop Q3 (.T(in_2), .clk(Q2_qn), .Q(Q0_q[3]), .reset(and_1_out));  // open: Qn, preset
  and and_1 (and_1_out, Q0_q[2], Q0_q[1]);
  T_Flip_Flop t_ff_4 (.T(in_4), .clk(t_ff_3_qn), .Q(t_ff_1_q[3]), .reset(out_7[1]));  // open: Qn, preset
  _4bit_mult_main main_1 (.A(in_1), .B(Q0_q), .out_3({main_1_out_3, out_5}));
  _4bit_mult_main main_2 (.A(in_3), .B(t_ff_1_q), .out_3({out_7, out_6}));
  Hex_Digit_Display hex_digit_display_1 (.value(out_5));  // open: dp
  Hex_Digit_Display hex_digit_display_2 (.value(out_7));  // open: dp
  Hex_Digit_Display hex_digit_display_3 (.value(out_6));  // open: dp
endmodule
